// Logisim project Decoder.circ as structural Verilog: 1 circuit, main circuit main
module main (
  input  Enable,
  input  GND,
  input  VCC,
  output out_4,
  output out_5,
  output out_6,
  output out_7,
  output out_8,
  output out_9,
  output out_10
);

  wire and_1_out, and_2_out, CLK_out, decoder_1_out0, decoder_1_out1, decoder_1_out2, decoder_1_out3,
       decoder_1_out4, decoder_1_out5, decoder_1_out6, decoder_1_out7, decoder_1_out8, decoder_1_out9,
       or_1_out, or_2_out, or_3_out, or_6_out, or_8_out, or_9_out, or_11_out, or_12_out, or_14_out,
       or_16_out, or_17_out, W, X, Y, Z;

  or or_1 (or_1_out, decoder_1_out0, decoder_1_out1, decoder_1_out2);
  Decoder #(.select(4)) decoder_1 (
    .out0(decoder_1_out0), .out1(decoder_1_out1), .out2(decoder_1_out2), .out3(decoder_1_out3),
    .out4(decoder_1_out4), .out5(decoder_1_out5), .out6(decoder_1_out6), .out7(decoder_1_out7),
    .out8(decoder_1_out8), .out9(decoder_1_out9), .sel({Z, Y, X, W}), .en(Enable));  // open: out10, out11, out12, out13, out14, out15
  or or_2 (or_2_out, decoder_1_out3, decoder_1_out4, decoder_1_out7);
  or or_3 (or_3_out, decoder_1_out3, decoder_1_out4, decoder_1_out5);
  or or_4 (out_4, or_1_out, or_2_out, decoder_1_out9);
  or or_5 (out_5, or_3_out, decoder_1_out9);
  and and_1 (and_1_out, Y, X, W);
  and and_2 (and_2_out, X, W);
  or or_6 (or_6_out, decoder_1_out1, decoder_1_out4, decoder_1_out5);
  or or_7 (out_6, or_6_out, decoder_1_out7, decoder_1_out9);
  Clock CLK (.out(CLK_out));
  or or_8 (or_8_out, decoder_1_out3, decoder_1_out4, decoder_1_out7);
  or or_9 (or_9_out, decoder_1_out0, decoder_1_out1, decoder_1_out2);
  or or_10 (out_7, or_9_out, or_8_out, decoder_1_out9);
  J_K_Flip_Flop j_k_ff_1 (.J(and_1_out), .clk(CLK_out), .K(and_1_out), .Q(Z), .reset(GND));  // open: Qn, preset, en
  J_K_Flip_Flop j_k_ff_2 (.J(and_2_out), .clk(CLK_out), .K(and_2_out), .Q(Y), .reset(GND));  // open: Qn, preset, en
  J_K_Flip_Flop j_k_ff_3 (.J(W), .clk(CLK_out), .K(W), .Q(X), .reset(GND));  // open: Qn, preset, en
  J_K_Flip_Flop j_k_ff_4 (.J(VCC), .clk(CLK_out), .K(VCC), .Q(W), .reset(GND));  // open: Qn, preset, en
  or or_11 (or_11_out, decoder_1_out0, decoder_1_out1, decoder_1_out2);
  or or_12 (or_12_out, decoder_1_out0, decoder_1_out2, decoder_1_out3);
  or or_13 (out_8, or_12_out, decoder_1_out7);
  or or_14 (or_14_out, decoder_1_out1, decoder_1_out2, decoder_1_out3);
  or or_15 (out_9, or_11_out, decoder_1_out7);
  or or_16 (or_16_out, decoder_1_out8, decoder_1_out9);
  or or_17 (or_17_out, decoder_1_out4, decoder_1_out6, decoder_1_out7);
  or or_18 (out_10, or_14_out, or_17_out, or_16_out);
  _7_Segment_Display u_7_segment_display_1 (
    .g(out_10), .f(out_9), .a(out_4), .b(out_5), .e(out_8), .d(out_7), .c(out_6));  // open: dp

  // Other names for the same wires on the sheet: a = out_4; b = out_5; c = out_6; d = out_7; e = out_8; f = out_9;
  //   g = out_10
endmodule
