// Logisim project Lab-Homework.circ as structural Verilog: 3 circuits, main circuit gate circuit
module gate_circuit (
  input  W,
  input  X,
  input  Y,
  input  Z,
  output a,
  output b,
  output c,
  output d,
  output e,
  output f,
  output g
);

  wire and_1_out, and_2_out, and_3_out, and_4_out, and_5_out, and_6_out, and_7_out, and_8_out, and_9_out,
       and_10_out, and_11_out, and_12_out, and_13_out, and_14_out, and_15_out, and_16_out, and_17_out,
       and_18_out, and_19_out, and_20_out, and_21_out, and_22_out, and_23_out, and_24_out, and_25_out,
       and_26_out, and_27_out, and_28_out, not_1_out, not_2_out, not_3_out, not_4_out, not_5_out, not_6_out,
       not_7_out, not_8_out, not_9_out, not_10_out, not_11_out, not_12_out, not_13_out, not_14_out,
       not_15_out, not_16_out, not_17_out, not_18_out, not_19_out, not_20_out, not_21_out, not_22_out,
       not_23_out, not_24_out, not_25_out, not_26_out, not_27_out, or_1_out, or_2_out, or_3_out, or_4_out,
       or_5_out, or_6_out, or_8_out, or_9_out, or_11_out;

  not not_1 (not_1_out, W);
  not not_2 (not_2_out, X);
  not not_3 (not_3_out, W);
  and and_1 (and_1_out, not_3_out, not_4_out);
  not not_4 (not_4_out, Y);
  not not_5 (not_5_out, Z);
  not not_6 (not_6_out, X);
  not not_7 (not_7_out, X);
  and and_2 (and_2_out, not_7_out, Y);
  not not_8 (not_8_out, Y);
  not not_9 (not_9_out, Y);
  and and_3 (and_3_out, not_9_out, Z);
  and and_4 (and_4_out, X, not_10_out);
  not not_10 (not_10_out, Y);
  not not_11 (not_11_out, W);
  not not_12 (not_12_out, X);
  not not_13 (not_13_out, W);
  and and_5 (and_5_out, not_13_out, not_14_out);
  not not_14 (not_14_out, Y);
  not not_15 (not_15_out, Z);
  not not_16 (not_16_out, X);
  not not_17 (not_17_out, W);
  and and_6 (and_6_out, not_17_out, not_18_out);
  not not_18 (not_18_out, X);
  not not_19 (not_19_out, Z);
  not not_20 (not_20_out, W);
  and and_7 (and_7_out, not_20_out, not_21_out);
  not not_21 (not_21_out, X);
  not not_22 (not_22_out, Y);
  not not_23 (not_23_out, W);
  and and_8 (and_8_out, not_23_out, not_24_out);
  not not_24 (not_24_out, X);
  not not_25 (not_25_out, Z);
  not not_26 (not_26_out, X);
  and and_9 (and_9_out, not_26_out, Z);
  and and_10 (and_10_out, X, not_27_out);
  not not_27 (not_27_out, Z);
  and and_11 (and_11_out, not_1_out, not_2_out);
  and and_12 (and_12_out, and_1_out, not_5_out);
  and and_13 (and_13_out, not_6_out, Z);
  and and_14 (and_14_out, Y, Z);
  and and_15 (and_15_out, and_2_out, Z);
  and and_16 (and_16_out, X, not_8_out);
  or or_1 (or_1_out, and_3_out, and_4_out);
  and and_17 (and_17_out, X, Z);
  and and_18 (and_18_out, not_11_out, not_12_out);
  and and_19 (and_19_out, and_5_out, not_15_out);
  and and_20 (and_20_out, not_16_out, Z);
  and and_21 (and_21_out, Y, Z);
  and and_22 (and_22_out, and_6_out, not_19_out);
  and and_23 (and_23_out, Y, Z);
  and and_24 (and_24_out, and_7_out, not_22_out);
  and and_25 (and_25_out, and_8_out, not_25_out);
  and and_26 (and_26_out, X, Y);
  or or_2 (or_2_out, and_9_out, Y);
  or or_3 (or_3_out, and_10_out, W);
  or or_4 (or_4_out, and_11_out, and_12_out);
  or or_5 (or_5_out, and_13_out, and_14_out);
  or or_6 (or_6_out, and_15_out, and_16_out);
  and and_27 (and_27_out, W, Z);
  or or_7 (c, or_1_out, and_17_out);
  or or_8 (or_8_out, and_18_out, and_19_out);
  or or_9 (or_9_out, and_20_out, and_21_out);
  or or_10 (e, and_22_out, and_23_out);
  or or_11 (or_11_out, and_24_out, and_25_out);
  and and_28 (and_28_out, and_26_out, Z);
  or or_12 (g, or_2_out, or_3_out);
  or or_13 (a, or_4_out, or_5_out);
  or or_14 (b, or_6_out, and_27_out);
  or or_15 (d, or_8_out, or_9_out);
  or or_16 (f, or_11_out, and_28_out);
  _7_Segment_Display u_7_segment_display_1 (.g(g), .f(f), .a(a), .b(b), .e(e), .d(d), .c(c));  // open: dp
endmodule

module dec_circuit (
  input  [3:0] WXYZ
);

  wire gate_circuit_1_a, gate_circuit_1_b, gate_circuit_1_c, gate_circuit_1_d, gate_circuit_1_e,
       gate_circuit_1_f, gate_circuit_1_g;

  gate_circuit gate_circuit_1 (
    .W(WXYZ[3]), .X(WXYZ[2]), .Y(WXYZ[1]), .Z(WXYZ[0]), .a(gate_circuit_1_a), .b(gate_circuit_1_b),
    .c(gate_circuit_1_c), .d(gate_circuit_1_d), .e(gate_circuit_1_e), .f(gate_circuit_1_f),
    .g(gate_circuit_1_g));
  _7_Segment_Display u_7_segment_display_1 (
    .g(gate_circuit_1_g), .f(gate_circuit_1_f), .a(gate_circuit_1_a), .b(gate_circuit_1_b),
    .e(gate_circuit_1_e), .d(gate_circuit_1_d), .c(gate_circuit_1_c));  // open: dp
endmodule

module Nand___NOR_part (
  input  W,
  input  X,
  input  Y,
  input  Z,
  output a,
  output b,
  output c,
  output d,
  output e,
  output f,
  output g
);

  wire nand_1_out, nand_2_out, nand_3_out, nand_4_out, nand_5_out, nand_6_out, nand_7_out, nand_8_out,
       nand_9_out, nand_10_out, nand_11_out, nand_12_out, nand_13_out, nand_14_out, nand_15_out, nand_16_out,
       nand_17_out, nand_18_out, nand_19_out, nand_20_out, nand_21_out, nand_22_out, nand_23_out,
       nand_24_out, nand_25_out, nand_26_out, nand_27_out, nand_28_out, nand_29_out, nand_30_out,
       nand_31_out, nand_32_out, nand_33_out, nand_34_out, nand_35_out, nand_36_out, nand_37_out,
       nand_38_out, nand_39_out, nand_40_out, nand_41_out, nand_42_out, nand_43_out, nand_44_out,
       nand_45_out, nand_46_out, nand_47_out, nand_48_out, nand_49_out, nand_50_out;

  nand nand_1 (nand_1_out, W, W);
  nand nand_2 (nand_2_out, X, X);
  nand nand_3 (nand_3_out, W, W);
  nand nand_4 (nand_4_out, Y, Y);
  nand nand_5 (nand_5_out, Z, Z);
  nand nand_6 (nand_6_out, X, X);
  nand nand_7 (nand_7_out, X, X);
  nand nand_8 (nand_8_out, Y, Y);
  nand nand_9 (nand_9_out, Y, Y);
  nand nand_10 (nand_10_out, Y, Y);
  nand nand_11 (nand_11_out, W, W);
  nand nand_12 (nand_12_out, X, X);
  nand nand_13 (nand_13_out, W, W);
  nand nand_14 (nand_14_out, Y, Y);
  nand nand_15 (nand_15_out, Z, Z);
  nand nand_16 (nand_16_out, X, X);
  nand nand_17 (nand_17_out, W, W);
  nand nand_18 (nand_18_out, X, X);
  nand nand_19 (nand_19_out, Z, Z);
  nand nand_20 (nand_20_out, W, W);
  nand nand_21 (nand_21_out, X, X);
  nand nand_22 (nand_22_out, Y, Y);
  nand nand_23 (nand_23_out, W, W);
  nand nand_24 (nand_24_out, X, X);
  nand nand_25 (nand_25_out, Z, Z);
  nand nand_26 (nand_26_out, X, X);
  nand nand_27 (nand_27_out, Z, Z);
  nand nand_28 (nand_28_out, nand_1_out, nand_2_out);
  nand nand_29 (nand_29_out, nand_3_out, nand_4_out, nand_5_out);
  nand nand_30 (nand_30_out, nand_6_out, Z);
  nand nand_31 (nand_31_out, Y, Z);
  nand nand_32 (nand_32_out, nand_7_out, Y, Z);
  nand nand_33 (nand_33_out, X, nand_8_out);
  nand nand_34 (nand_34_out, W, Z);
  nand nand_35 (nand_35_out, nand_9_out, Z);
  nand nand_36 (nand_36_out, X, nand_10_out);
  nand nand_37 (nand_37_out, X, Z);
  nand nand_38 (nand_38_out, nand_11_out, nand_12_out);
  nand nand_39 (nand_39_out, nand_13_out, nand_14_out, nand_15_out);
  nand nand_40 (nand_40_out, nand_16_out, Z);
  nand nand_41 (nand_41_out, Y, Z);
  nand nand_42 (nand_42_out, nand_17_out, nand_18_out, nand_19_out);
  nand nand_43 (nand_43_out, Y, Z);
  nand nand_44 (nand_44_out, nand_20_out, nand_21_out, nand_22_out);
  nand nand_45 (nand_45_out, nand_23_out, nand_24_out, nand_25_out);
  nand nand_46 (nand_46_out, X, Y, Z);
  nand nand_47 (nand_47_out, nand_26_out, Z);
  nand nand_48 (nand_48_out, Y, Y);
  nand nand_49 (nand_49_out, X, nand_27_out);
  nand nand_50 (nand_50_out, W, W);
  nand nand_51 (a, nand_28_out, nand_29_out, nand_30_out, nand_31_out);
  nand nand_52 (b, nand_32_out, nand_33_out, nand_34_out);
  nand nand_53 (c, nand_35_out, nand_36_out, nand_37_out);
  nand nand_54 (d, nand_38_out, nand_39_out, nand_40_out, nand_41_out);
  nand nand_55 (e, nand_42_out, nand_43_out);
  nand nand_56 (f, nand_44_out, nand_45_out, nand_46_out);
  nand nand_57 (g, nand_47_out, nand_48_out, nand_49_out, nand_50_out);
  _7_Segment_Display u_7_segment_display_1 (.g(g), .f(f), .a(a), .b(b), .e(e), .d(d), .c(c));  // open: dp
endmodule
